// Logisim project BreadboardComputer.circ as structural Verilog: 1 circuit, main circuit main
module main (
);

  wire [7:0] fpnegator_1_p1;

  _7421 u_7421_1 ();  // open: pin1, pin2, pin3, pin4, pin5, pin6, pin13, pin12, pin11, pin10, pin9, pin8
  _7418 u_7418_1 ();  // open: pin1, pin2, pin3, pin4, pin5, pin6, pin13, pin12, pin11, pin10, pin9, pin8
  _7430 u_7430_1 ();  // open: pin1, pin2, pin3, pin4, pin5, pin6, pin13, pin12, pin11, pin10, pin9, pin8
  FPMultiplier fpmultiplier_1 ();  // open: a, b, out
  _7430 u_7430_2 ();  // open: pin1, pin2, pin3, pin4, pin5, pin6, pin13, pin12, pin11, pin10, pin9, pin8
  _7421 u_7421_2 ();  // open: pin1, pin2, pin3, pin4, pin5, pin6, pin13, pin12, pin11, pin10, pin9, pin8
  BitFinder bitfinder_1 ();  // open: in, index, found
  Adder adder_1 (.a(fpnegator_1_p1));  // open: b, out, cin, cout
  // FPNegator fpnegator_1: pin names not known; wires that end beside it: fpnegator_1_p1, fpnegator_1_p1, fpnegator_1_p1
  _7411 u_7411_1 ();  // open: pin1, pin2, pin3, pin4, pin5, pin6, pin13, pin12, pin11, pin10, pin9, pin8
  FPMultiplier fpmultiplier_2 ();  // open: a, b, out
  _7414 u_7414_1 ();  // open: pin1, pin2, pin3, pin4, pin5, pin6, pin13, pin12, pin11, pin10, pin9, pin8
  Comparator comparator_1 (.eq(fpnegator_1_p1[0]));  // open: a, b, gt, lt
  _7411 u_7411_2 ();  // open: pin1, pin2, pin3, pin4, pin5, pin6, pin13, pin12, pin11, pin10, pin9, pin8
  _7421 u_7421_3 ();  // open: pin1, pin2, pin3, pin4, pin5, pin6, pin13, pin12, pin11, pin10, pin9, pin8
  Clock clock_1 (.out(fpnegator_1_p1[0]));
  // RGBLED rgbled_1: pin names not known; wires that end beside it: fpnegator_1_p1, fpnegator_1_p1, fpnegator_1_p1
  // Pins of 1 and 8 bits meet at fpnegator_1_p1
endmodule
