// Logisim project CPU.circ as structural Verilog
module Breadboard_template (
);


  // Notes on the sheet:
  //   10
  //   10
  //   20
  //   20
  //   30
  //   30
  //   40
  //   40
  //   50
  //   50
  //   60
  //   60
endmodule
