// Logisim project ALU.circ as structural Verilog
module ALU (
  input  [15:0] input_a,
  input  [15:0] input_b,
  input  in_3,
  input  [1:0] in_4,
  input  in_5,
  input  [15:0] in_6,
  input  [15:0] in_7,
  input  in_8,
  input  [1:0] in_9,
  output cFlag,
  output [15:0] out_11,
  output nFlag,
  output zFlag
);

  wire demultiplexer_1_out1, demultiplexer_1_out2, demultiplexer_1_out3, demultiplexer_2_out1,
       demultiplexer_2_out2, demultiplexer_2_out3, not_1_out;
  wire [15:0] adder_1_out, adder_2_out, controlled_buffer_1_out, controlled_buffer_3_out, nand_1_out,
       nand_2_out, xor_1_out, xor_2_out;

  assign xor_1_out = input_a ^ input_b;  // XOR_Gate xor_1, 16 bits wide
  assign controlled_buffer_1_out = demultiplexer_2_out3 ? xor_1_out : 16'bz;  // Controlled_Buffer controlled_buffer_1
  assign {nFlag, out_11[14:0]} = not_1_out ? controlled_buffer_1_out : 16'bz;  // Controlled_Buffer controlled_buffer_2
  assign xor_2_out = in_6 ^ in_7;  // XOR_Gate xor_2, 16 bits wide
  assign controlled_buffer_3_out = demultiplexer_1_out1 ? xor_2_out : 16'bz;  // Controlled_Buffer controlled_buffer_3
  assign nand_1_out = ~(input_b & input_a);  // NAND_Gate nand_1, 16 bits wide
  assign controlled_buffer_1_out = demultiplexer_2_out2 ? adder_2_out : 16'bz;  // Controlled_Buffer controlled_buffer_4
  assign controlled_buffer_1_out = demultiplexer_2_out1 ? nand_1_out : 16'bz;  // Controlled_Buffer controlled_buffer_5
  assign nand_2_out = ~(in_6 & in_7);  // NAND_Gate nand_2, 16 bits wide
  assign controlled_buffer_3_out = demultiplexer_1_out2 ? nand_2_out : 16'bz;  // Controlled_Buffer controlled_buffer_6
  Adder #(.width(16)) adder_1 (.a(in_6), .b(in_7), .out(adder_1_out));  // open: cin, cout
  Adder #(.width(16)) adder_2 (.a(input_b), .b(input_a), .out(adder_2_out), .cout(cFlag));  // open: cin
  assign {nFlag, out_11[14:0]} = in_5 ? {1'b0, controlled_buffer_1_out[15:1]} : 16'bz;  // Controlled_Buffer controlled_buffer_7
  assign controlled_buffer_3_out = demultiplexer_1_out3 ? adder_1_out : 16'bz;  // Controlled_Buffer controlled_buffer_8
  not not_1 (not_1_out, in_5);
  Demultiplexer #(.select(2)) demultiplexer_1 (
    .out1(demultiplexer_1_out1), .out2(demultiplexer_1_out2), .out3(demultiplexer_1_out3), .in(in_8),
    .sel(in_9));  // open: out0
  Demultiplexer #(.select(2)) demultiplexer_2 (
    .out1(demultiplexer_2_out1), .out2(demultiplexer_2_out2), .out3(demultiplexer_2_out3), .in(in_3),
    .sel(in_4));  // open: out0
  nor nor_1 (zFlag, out_11[8], nFlag, out_11[14], out_11[13], out_11[12], out_11[11], out_11[10], out_11[9], out_11[7], out_11[6], out_11[5], out_11[4], out_11[3], out_11[2], out_11[1], out_11[0]);

  assign out_11[15] = nFlag;
endmodule
