// Logisim project Decoding.circ as structural Verilog: 1 circuit, main circuit main
module main (
  input  [14:0] in_1
);

  wire [7:0] rom_1_data;

  Register register_1 ();  // open: D, en, clk, Q, clr
  ROM #(.addrWidth(15)) rom_1 (.addr(in_1), .data(rom_1_data));
endmodule
