// Logisim project alu_perfekt.circ as structural Verilog: 3 circuits, main circuit main
module main (
  input  [1:0] in_1
);

  wire CLK;
  wire [15:0] alu_1_aluout, DATA;

  Clock clock_1 (.out(CLK));
  ALU alu_1 (
    .CLK(CLK), .DATA(DATA), .InstrBus(in_1), .aluOut(alu_1_aluout));  // open: WALUb, WALUa, cIn, LSR, cFlag, eFlag, nFlag, zFlag
  Registere registere_1 (.ALU(alu_1_aluout));  // open: AO, CLK, ADRESSEBUSS, WA, IRO, DATABUSS, MARO, WD, ID, BO, WB, CO, WC, DO, PO, SO, WS, MDRO, WMDR, DATA

  // Notes on the sheet:
  //   Registere kunne egt ha vært en god Main
  //   Skulle ikke aluOut bare gjennom databussen? Blir mye mindre kabling, selv om kanskje fler sykluser per instruksjon
endmodule

module Registere (
  input  AO,
  input  CLK,
  input  [15:0] ADRESSEBUSS,
  input  WA,
  input  IRO,
  input  [15:0] DATABUSS,
  input  MARO,
  input  WD,
  input  [15:0] ID,
  input  BO,
  input  WB,
  input  CO,
  input  WC,
  input  DO,
  input  PO,
  input  [15:0] ALU,
  input  SO,
  input  WS,
  input  MDRO,
  input  WMDR,
  output [15:0] DATA
);

  wire not_1_out, not_2_out, not_3_out, not_4_out, not_5_out, not_6_out, not_7_out, not_8_out, not_9_out,
       undriven;
  wire [15:0] counter_1_q, RAM, register_1_q, register_2_q, register_3_q, register_4_q, register_5_q,
       register_6_q, register_7_q, register_8_q;

  Register #(.width(16)) register_1 (.D(DATABUSS), .en(WB), .clk(CLK), .Q(register_1_q));  // open: clr
  Register #(.width(16)) register_2 (.D(DATABUSS), .en(WC), .clk(CLK), .Q(register_2_q));  // open: clr
  Register #(.width(16)) register_3 (.D(DATABUSS), .en(WD), .clk(CLK), .Q(register_3_q));  // open: clr
  Register #(.width(16)) register_4 (.D(DATABUSS), .en(WA), .clk(CLK), .Q(register_4_q));  // open: clr
  Register #(.width(16)) register_5 (.D(ALU), .en(WS), .clk(CLK), .Q(register_5_q));  // open: clr
  Register #(.width(16)) register_6 (.D(RAM), .en(WMDR), .clk(CLK), .Q(register_6_q));  // open: clr
  not not_1 (not_1_out, AO);
  Transistor #(.width(16)) transistor_1 (.in(register_4_q), .out(DATABUSS), .gate(not_1_out));
  not not_2 (not_2_out, BO);
  Transistor #(.width(16)) transistor_2 (.in(register_1_q), .out(DATABUSS), .gate(not_2_out));
  not not_3 (not_3_out, CO);
  Transistor #(.width(16)) transistor_3 (.in(register_2_q), .out(DATABUSS), .gate(not_3_out));
  not not_4 (not_4_out, DO);
  Transistor #(.width(16)) transistor_4 (.in(register_3_q), .out(DATABUSS), .gate(not_4_out));
  not not_5 (not_5_out, SO);
  Transistor #(.width(16)) transistor_5 (.in(register_5_q), .out(DATABUSS), .gate(not_5_out));
  not not_6 (not_6_out, MDRO);
  Transistor #(.width(16)) transistor_6 (.in(register_6_q), .out(DATABUSS), .gate(not_6_out));
  Register #(.width(16)) register_7 (.D(DATABUSS), .en(WD), .clk(CLK), .Q(register_7_q));  // open: clr
  not not_7 (not_7_out, IRO);
  Transistor #(.width(16)) transistor_7 (.in(register_7_q), .out(ID), .gate(not_7_out));
  Counter #(.max('hffff), .width(16)) counter_1 (
    .load(undriven), .clk(CLK), .Q(counter_1_q));  // open: clr, up, count, D, carry
  not not_8 (not_8_out, PO);
  Transistor #(.width(16)) transistor_8 (.in(counter_1_q), .out(ADRESSEBUSS), .gate(not_8_out));
  Register #(.width(16)) register_8 (.D(ADRESSEBUSS), .en(WD), .clk(CLK), .Q(register_8_q));  // open: clr
  not not_9 (not_9_out, MARO);
  Transistor #(.width(16)) transistor_9 (.in(register_8_q), .out(ADRESSEBUSS), .gate(not_9_out));

  assign DATA = DATABUSS;

  // Notes on the sheet:
  //   Hvorfor bruker denne WD?
  //   La ikke WD til som input i tilfelle dette funker annenleder fra de andre
  //   ??? Treng dette inputs i circen?
  //   Sparer vi ikke sykluser på  å  loade direkte til databuss? Blir mindre komplisert, siden vi ikke har snakket om noe cashing
endmodule

module ALU (
  input  CLK,
  input  WALUb,
  input  [15:0] DATA,
  input  WALUa,
  input  cIn,
  input  [1:0] InstrBus,
  input  LSR,
  output cFlag,
  output eFlag,
  output [15:0] aluOut,
  output nFlag,
  output zFlag
);

  wire demultiplexer_1_out1, demultiplexer_1_out2, demultiplexer_1_out3, not_1_out;
  wire [15:0] adder_1_out, ALU_a_q, ALU_b_q, nand_1_out, xor_1_out;
  wire [15:1] controlled_buffer_1_out;

  Register #(.width(16)) ALU_a (.D(DATA), .en(WALUa), .clk(CLK), .Q(ALU_a_q));  // open: clr
  assign xor_1_out = ALU_a_q ^ ALU_b_q;  // XOR_Gate xor_1, 16 bits wide
  assign {controlled_buffer_1_out, eFlag} = demultiplexer_1_out3 ? xor_1_out : 16'bz;  // Controlled_Buffer controlled_buffer_1
  assign aluOut = not_1_out ? {controlled_buffer_1_out, eFlag} : 16'bz;  // Controlled_Buffer controlled_buffer_2
  Register #(.width(16)) ALU_b (.D(DATA), .en(WALUb), .clk(CLK), .Q(ALU_b_q));  // open: clr
  assign nand_1_out = ~(ALU_b_q & ALU_a_q);  // NAND_Gate nand_1, 16 bits wide
  assign {controlled_buffer_1_out, eFlag} = demultiplexer_1_out2 ? adder_1_out : 16'bz;  // Controlled_Buffer controlled_buffer_3
  assign {controlled_buffer_1_out, eFlag} = demultiplexer_1_out1 ? nand_1_out : 16'bz;  // Controlled_Buffer controlled_buffer_4
  Adder #(.width(16)) adder_1 (.a(ALU_b_q), .b(ALU_a_q), .out(adder_1_out), .cin(cIn), .cout(cFlag));
  assign aluOut = LSR ? {1'b0, controlled_buffer_1_out} : 16'bz;  // Controlled_Buffer controlled_buffer_5
  not not_1 (not_1_out, LSR);
  Demultiplexer #(.select(2)) demultiplexer_1 (
    .out1(demultiplexer_1_out1), .out2(demultiplexer_1_out2), .out3(demultiplexer_1_out3), .in(CLK),
    .sel(InstrBus));  // open: out0
  nor nor_1 (zFlag, aluOut[8], aluOut[15], aluOut[14], aluOut[13], aluOut[12], aluOut[11], aluOut[10], aluOut[9], aluOut[7], aluOut[6], aluOut[5], aluOut[4], aluOut[3], aluOut[2], aluOut[1], aluOut[0]);

  assign nFlag = aluOut[15];

  // Notes on the sheet:
  //   Even flag kan slettes om den ikke trengs
endmodule
