// Logisim project JMPLogic.circ as structural Verilog: 1 circuit, main circuit main
module main (
  input  JZ,
  input  JN,
  input  JC,
  input  J,
  input  Z,
  input  N,
  input  C,
  output LoadPC
);

  wire and_1_out, and_2_out, and_3_out;

  and and_1 (and_1_out, JZ, Z);
  and and_2 (and_2_out, JN, N);
  and and_3 (and_3_out, JC, C);
  or or_1 (LoadPC, J, and_1_out, and_2_out, and_3_out);
endmodule
