// Logisim project RegisterDecoding.circ as structural Verilog: 1 circuit, main circuit main
module main (
  input  srcBE,
  input  srcAE,
  input  destL,
  input  dest1,
  input  dest2,
  input  dest3,
  input  srcA1,
  input  srcA2,
  input  srcA3,
  input  srcB1,
  input  srcB2,
  input  srcB3,
  output R0Load,
  output R1Load,
  output R2Load,
  output R3Load,
  output R4Load,
  output R5Load,
  output R6Load,
  output R7Load,
  output R0EInv,
  output R1EInv,
  output R2EInv,
  output R3EInv,
  output R4EInv,
  output R5EInv,
  output R6EInv,
  output R7EInv
);

  wire n74138_1_pin4, n74138_1_pin7, n74138_1_pin9, n74138_1_pin10, n74138_1_pin11, n74138_1_pin12,
       n74138_1_pin13, n74138_1_pin14, n74138_1_pin15, n74138_2_pin4, n74138_2_pin7, n74138_2_pin9,
       n74138_2_pin10, n74138_2_pin11, n74138_2_pin12, n74138_2_pin13, n74138_2_pin14, n74138_2_pin15,
       n74138_3_pin4, n74138_3_pin7, n74138_3_pin9, n74138_3_pin10, n74138_3_pin11, n74138_3_pin12,
       n74138_3_pin13, n74138_3_pin14, n74138_3_pin15;

  _74138 u_74138_1 (
    .pin1(dest1), .pin2(dest2), .pin3(dest3), .pin4(n74138_1_pin4), .pin5(n74138_1_pin4), .pin6(destL),
    .pin7(n74138_1_pin7), .pin15(n74138_1_pin15), .pin14(n74138_1_pin14), .pin13(n74138_1_pin13),
    .pin12(n74138_1_pin12), .pin11(n74138_1_pin11), .pin10(n74138_1_pin10), .pin9(n74138_1_pin9));
  _74138 u_74138_2 (
    .pin1(srcA1), .pin2(srcA2), .pin3(srcA3), .pin4(n74138_2_pin4), .pin5(n74138_2_pin4), .pin6(srcAE),
    .pin7(n74138_2_pin7), .pin15(n74138_2_pin15), .pin14(n74138_2_pin14), .pin13(n74138_2_pin13),
    .pin12(n74138_2_pin12), .pin11(n74138_2_pin11), .pin10(n74138_2_pin10), .pin9(n74138_2_pin9));
  _74138 u_74138_3 (
    .pin1(srcB1), .pin2(srcB2), .pin3(srcB3), .pin4(n74138_3_pin4), .pin5(n74138_3_pin4), .pin6(srcBE),
    .pin7(n74138_3_pin7), .pin15(n74138_3_pin15), .pin14(n74138_3_pin14), .pin13(n74138_3_pin13),
    .pin12(n74138_3_pin12), .pin11(n74138_3_pin11), .pin10(n74138_3_pin10), .pin9(n74138_3_pin9));
  not not_1 (R0Load, n74138_1_pin15);
  not not_2 (R1Load, n74138_1_pin14);
  not not_3 (R2Load, n74138_1_pin13);
  not not_4 (R3Load, n74138_1_pin12);
  not not_5 (R4Load, n74138_1_pin11);
  not not_6 (R5Load, n74138_1_pin10);
  not not_7 (R6Load, n74138_1_pin9);
  not not_8 (R7Load, n74138_1_pin7);
  and and_1 (R0EInv, n74138_2_pin15, n74138_3_pin15);
  and and_2 (R1EInv, n74138_2_pin14, n74138_3_pin14);
  and and_3 (R2EInv, n74138_2_pin13, n74138_3_pin13);
  and and_4 (R3EInv, n74138_2_pin12, n74138_3_pin12);
  and and_5 (R4EInv, n74138_2_pin11, n74138_3_pin11);
  and and_6 (R5EInv, n74138_2_pin10, n74138_3_pin10);
  and and_7 (R6EInv, n74138_2_pin9, n74138_3_pin9);
  and and_8 (R7EInv, n74138_2_pin7, n74138_3_pin7);
  // also tied to GND on the sheet: {n74138_1_pin4, n74138_2_pin4, n74138_3_pin4}

  // Notes on the sheet:
  //   Dest. reg. bits from the instruction
  //   Source A reg. bits from the instruction
  //   Source B reg. bits from the instruction
  //   Note: The 74xy138-DMXs have active-low outputs
  //   Note: The control unit decides when to activate each of the demultiplexers
  //   Either srcAE or srcBE is 1 whenever the control unit decides to enable one of the source registers
  //   destL (Destination Load) is 1 if the control unit decides to load the destination register
  //   Note: This circuit assumes that at most one register should output be enabled at a time. It contains no fail-safe for erroneous outputs from the instruction decoder.
  //   Active-high load lines, one for each register
  //   Active-low enable lines, one for each register
endmodule
