// Logisim project Registere.circ as structural Verilog: 1 circuit, main circuit main
module main (
  input  in_1,
  input  in_2,
  input  in_3,
  input  in_4,
  input  in_5,
  input  in_6,
  input  in_7,
  input  in_8,
  input  in_9
);

  wire CLK, COUNTDIR, LOADPC, not_1_out, not_2_out, not_3_out, not_4_out, not_5_out, not_6_out, not_7_out,
       not_8_out, not_9_out, WA, WB, WC, WD, WMDR, WS;
  wire [15:0] ADRESSEBUSS, ALU, counter_1_q, DATABUSS, ID, IMPC, register_1_q, register_2_q, register_3_q,
       register_4_q, register_5_q, register_6_q, register_7_q, register_8_q;

  Clock clock_1 (.out(CLK));
  Register #(.width(16)) register_1 (.D(DATABUSS), .en(WB), .clk(CLK), .Q(register_1_q));  // open: clr
  Register #(.width(16)) register_2 (.D(DATABUSS), .en(WC), .clk(CLK), .Q(register_2_q));  // open: clr
  Register #(.width(16)) register_3 (.D(DATABUSS), .en(WD), .clk(CLK), .Q(register_3_q));  // open: clr
  Register #(.width(16)) register_4 (.D(DATABUSS), .en(WA), .clk(CLK), .Q(register_4_q));  // open: clr
  Register #(.width(16)) register_5 (.D(ALU), .en(WS), .clk(CLK), .Q(register_5_q));  // open: clr
  Register #(.width(16)) register_6 (.D(ADRESSEBUSS), .en(WMDR), .clk(CLK), .Q(register_6_q));  // open: clr
  not not_1 (not_1_out, in_1);
  Transistor #(.width(16)) transistor_1 (.in(register_4_q), .out(DATABUSS), .gate(not_1_out));
  not not_2 (not_2_out, in_4);
  Transistor #(.width(16)) transistor_2 (.in(register_1_q), .out(DATABUSS), .gate(not_2_out));
  not not_3 (not_3_out, in_5);
  Transistor #(.width(16)) transistor_3 (.in(register_2_q), .out(DATABUSS), .gate(not_3_out));
  not not_4 (not_4_out, in_6);
  Transistor #(.width(16)) transistor_4 (.in(register_3_q), .out(DATABUSS), .gate(not_4_out));
  not not_5 (not_5_out, in_8);
  Transistor #(.width(16)) transistor_5 (.in(register_5_q), .out(DATABUSS), .gate(not_5_out));
  not not_6 (not_6_out, in_9);
  Transistor #(.width(16)) transistor_6 (.in(register_6_q), .out(DATABUSS), .gate(not_6_out));
  Register #(.width(16)) register_7 (.D(DATABUSS), .en(WD), .clk(CLK), .Q(register_7_q));  // open: clr
  not not_7 (not_7_out, in_2);
  Transistor #(.width(16)) transistor_7 (.in(register_7_q), .out(ID), .gate(not_7_out));
  Counter #(.max('hffff), .width(16)) counter_1 (
    .load(LOADPC), .up(COUNTDIR), .clk(CLK), .D(IMPC), .Q(counter_1_q));  // open: clr, count, carry
  not not_8 (not_8_out, in_7);
  Transistor #(.width(16)) transistor_8 (.in(counter_1_q), .out(ADRESSEBUSS), .gate(not_8_out));
  Register #(.width(16)) register_8 (.D(ADRESSEBUSS), .en(WD), .clk(CLK), .Q(register_8_q));  // open: clr
  not not_9 (not_9_out, in_3);
  Transistor #(.width(16)) transistor_9 (.in(register_8_q), .out(ADRESSEBUSS), .gate(not_9_out));

  // Other names for the same wires on the sheet: AO = in_1; BO = in_4; CO = in_5; DO = in_6; IRO = in_2; MARO = in_3;
  //   MDRO = in_9; PO = in_7; RAM[15:0] = ADRESSEBUSS; SO = in_8
endmodule
