// Logisim project Integrasjon.circ as structural Verilog
module alu_1 (
  input  WALUa,
  input  CLK,
  input  WALUb,
  input  [15:0] DATA,
  input  cIn,
  input  [1:0] InstrBus,
  input  LSR,
  output cFlag,
  output eFlag,
  output [15:0] aluOut,
  output nFlag,
  output zFlag
);

  wire demultiplexer_1_out1, demultiplexer_1_out2, demultiplexer_1_out3, not_1_out;
  wire [15:0] adder_1_out, ALU_a_q, ALU_b_q, nand_1_out, xor_1_out;
  wire [15:1] controlled_buffer_1_out;

  Register #(.width(16)) ALU_a (.D(DATA), .en(WALUa), .clk(CLK), .Q(ALU_a_q));  // open: clr
  assign xor_1_out = ALU_a_q ^ ALU_b_q;  // XOR_Gate xor_1, 16 bits wide
  assign {controlled_buffer_1_out, eFlag} = demultiplexer_1_out3 ? xor_1_out : 16'bz;  // Controlled_Buffer controlled_buffer_1
  assign aluOut = not_1_out ? {controlled_buffer_1_out, eFlag} : 16'bz;  // Controlled_Buffer controlled_buffer_2
  Register #(.width(16)) ALU_b (.D(DATA), .en(WALUb), .clk(CLK), .Q(ALU_b_q));  // open: clr
  assign nand_1_out = ~(ALU_b_q & ALU_a_q);  // NAND_Gate nand_1, 16 bits wide
  assign {controlled_buffer_1_out, eFlag} = demultiplexer_1_out2 ? adder_1_out : 16'bz;  // Controlled_Buffer controlled_buffer_3
  assign {controlled_buffer_1_out, eFlag} = demultiplexer_1_out1 ? nand_1_out : 16'bz;  // Controlled_Buffer controlled_buffer_4
  Adder #(.width(16)) adder_1 (.a(ALU_a_q), .b(ALU_b_q), .out(adder_1_out), .cin(cIn), .cout(cFlag));
  assign aluOut = LSR ? {1'b0, controlled_buffer_1_out} : 16'bz;  // Controlled_Buffer controlled_buffer_5
  not not_1 (not_1_out, LSR);
  Demultiplexer #(.select(2)) demultiplexer_1 (
    .out1(demultiplexer_1_out1), .out2(demultiplexer_1_out2), .out3(demultiplexer_1_out3), .in(CLK),
    .sel(InstrBus));  // open: out0
  nor nor_1 (zFlag, aluOut[8], aluOut[15], aluOut[14], aluOut[13], aluOut[12], aluOut[11], aluOut[10], aluOut[9], aluOut[7], aluOut[6], aluOut[5], aluOut[4], aluOut[3], aluOut[2], aluOut[1], aluOut[0]);

  assign nFlag = aluOut[15];

  // Notes on the sheet:
  //   Even flag kan slettes om den ikke trengs
  //   Endrer shift right til å være på samme nivå som xor, and og add så vi slipper en ledning
  //   11 = Xor
  //   00 = ingenting
  //   01 = nand
  //   10 = adder
endmodule

module registere_1 (
  input  AO,
  input  [3:0] SkalTilDekoding,
  input  CLK,
  input  [15:0] ADRESSEIN,
  input  AW,
  input  IRO,
  input  [15:0] DATAIN,
  input  [11:0] ID,
  input  IRW,
  input  BO,
  input  BW,
  input  DATAINENABLE,
  input  CountE,
  input  CounterO,
  input  [15:0] CounterJump,
  input  SumO,
  output [15:0] DATAOUT,
  output [15:0] ADRESSEOUT
);

  wire not_1_out, not_2_out, not_3_out, not_4_out, not_6_out, not_7_out, not_8_out, undriven, undriven_2,
       undriven_3, undriven_5, undriven_6, undriven_7, undriven_9, undriven_10;
  wire [15:0] controlled_buffer_1_out, controlled_buffer_2_out, counter_1_q, RAM, register_1_q, register_2_q,
       register_3_q, register_4_q, register_5_q, register_6_q, register_7_q, register_8_q, register_9_q,
       transistor_1_out, transistor_2_out, transistor_7_out, undriven_4, undriven_8;

  assign controlled_buffer_1_out = AW ? DATAOUT : 16'bz;  // Controlled_Buffer controlled_buffer_1
  Register #(.width(16)) register_1 (.D(controlled_buffer_2_out), .en(BW), .clk(CLK), .Q(register_1_q));  // open: clr
  assign controlled_buffer_2_out = BW ? DATAOUT : 16'bz;  // Controlled_Buffer controlled_buffer_2
  Register #(.width(16)) register_2 (.D(DATAOUT), .en(undriven_2), .clk(CLK), .Q(register_2_q));  // open: clr
  Register #(.width(16)) register_3 (.D(DATAOUT), .en(undriven), .clk(CLK), .Q(register_3_q));  // open: clr
  Register #(.width(16)) register_4 (.D(undriven_4), .en(1'b1), .clk(CLK), .Q(register_4_q));  // open: clr
  Register #(.width(16)) register_5 (.D(RAM), .en(undriven_3), .clk(CLK), .Q(register_5_q));  // open: clr
  Register #(.width(16)) register_6 (.D(controlled_buffer_1_out), .en(AW), .clk(CLK), .Q(register_6_q));  // open: clr
  assign DATAOUT = BO ? register_1_q : 16'bz;  // Controlled_Buffer controlled_buffer_3
  not not_1 (not_1_out, undriven_5);
  Transistor #(.width(16)) transistor_1 (.in(register_2_q), .out(transistor_1_out), .gate(not_1_out));
  not not_2 (not_2_out, undriven_6);
  Transistor #(.width(16)) transistor_2 (.in(register_3_q), .out(transistor_2_out), .gate(not_2_out));
  not not_3 (not_3_out, SumO);
  Transistor #(.width(16)) transistor_3 (.in(register_4_q), .out(DATAOUT), .gate(not_3_out));
  not not_4 (not_4_out, undriven_7);
  Transistor #(.width(16)) transistor_4 (.in(register_5_q), .gate(not_4_out));  // open: out
  assign DATAOUT = AO ? register_6_q : 16'bz;  // Controlled_Buffer controlled_buffer_4
  Register #(.width(16)) register_7 (.D(DATAOUT), .en(IRW), .clk(CLK), .Q(register_7_q));  // open: clr
  assign ADRESSEIN[15:12] = ~4'b1111;  // NOT_Gate not_5, 4 bits wide
  not not_6 (not_6_out, IRO);
  Transistor #(.width(16)) transistor_5 (.in(register_7_q), .out({SkalTilDekoding, ADRESSEIN[11:0]}), .gate(not_6_out));
  Register #(.width(16)) register_8 (.D(DATAIN), .en(DATAINENABLE), .clk(CLK), .Q(register_8_q));  // open: clr
  Counter #(.max('hffff), .width(16)) counter_1 (
    .load(CountE), .clk(CLK), .D(CounterJump), .Q(counter_1_q));  // open: clr, up, count, carry
  assign DATAOUT = DATAINENABLE ? register_8_q : 16'bz;  // Controlled_Buffer controlled_buffer_5
  not not_7 (not_7_out, CounterO);
  Transistor #(.width(16)) transistor_6 (.in(counter_1_q), .out(ADRESSEIN), .gate(not_7_out));
  Register #(.width(16)) register_9 (.D(undriven_8), .en(undriven_9), .clk(CLK), .Q(register_9_q));  // open: clr
  not not_8 (not_8_out, undriven_10);
  Transistor #(.width(16)) transistor_7 (.in(register_9_q), .out(transistor_7_out), .gate(not_8_out));

  assign ADRESSEOUT = ADRESSEIN;

  // Other names for the same wires on the sheet: ADRESSEBUSS[15:0] = ADRESSEIN; DATABUSS[15:0] = DATAOUT;
  //   DATABUSSIN[15:0] = DATAIN

  // Notes on the sheet:
  //   Under constrution!!
  //   Hvorfor bruker denne WD?
  //   La ikke WD til som input i tilfelle dette funker annenleder fra de andre
  //   Sparer vi ikke sykluser på  å  loade direkte til databuss? Blir mindre komplisert, siden vi ikke har snakket om noe cashing
  //   ??? Treng dette inputs i circen?
  //   Liten buffer siden det kommer feil når input pin er direkte koblet med en output pin
endmodule

module control_unit1 (
  input  CLK,
  input  SumO,
  input  CountJump,
  input  CountO,
  input  CountE,
  input  BW,
  input  BO,
  input  IRW,
  input  IRO,
  input  AW,
  input  AO,
  input  [3:0] Instruction
);

  wire CLK_t, not_2_out, RESET;
  wire [2:0] counter_1_q;
  wire [7:0] demultiplexer_1_out0;

  not not_1 (CLK_t, CLK);
  Counter #(.max('h7), .width(3)) counter_1 (
    .clr(RESET), .load(not_2_out), .up(1'b1), .clk(CLK_t), .Q(counter_1_q));  // open: count, D, carry
  not not_2 (not_2_out, 1'b1);
  Demultiplexer #(.select(3)) demultiplexer_1 (
    .out0(demultiplexer_1_out0[0]), .out1(demultiplexer_1_out0[1]), .out2(demultiplexer_1_out0[2]),
    .out3(demultiplexer_1_out0[3]), .out4(demultiplexer_1_out0[4]), .out5(demultiplexer_1_out0[5]),
    .out6(demultiplexer_1_out0[6]), .out7(demultiplexer_1_out0[7]), .in(1'b1), .sel(counter_1_q));
  ROM #(.addrWidth(12), .dataWidth(10)) rom_1 (
    .addr({Instruction, demultiplexer_1_out0}),
    .data({SumO, CountJump, CountO, CountE, BW, BO, IRW, IRO, AW, AO}));
endmodule

module main_1 (
);

  alu_1 alu_1_1 ();  // open: WALUa, CLK, WALUb, DATA, cIn, InstrBus, LSR, cFlag, eFlag, aluOut, nFlag, zFlag
endmodule

module registere_2 (
  input  LESE_SKRIVE_TIL_BUSS,
  input  CLK,
  input  [2:0] output_register_selection,
  input  [2:0] Write_register_selection,
  output IR_O,
  output IR_W,
  output [15:0] DATA_BUS
);

  wire A_O, A_W, ADR_O, ADR_W, B_O, B_W, PC_O, PC_W, R_O, R_W;
  wire [15:0] counter_1_1_adressout, ram_1_dout, register_1_q, register_2_q, register_3_q;

  Register #(.width(16)) register_1 (.D(DATA_BUS), .en(A_W), .clk(CLK), .Q(register_1_q));  // open: clr
  Register #(.width(16)) register_2 (.D(DATA_BUS), .en(B_W), .clk(CLK), .Q(register_2_q));  // open: clr
  assign DATA_BUS = A_O ? register_1_q : 16'bz;  // Controlled_Buffer controlled_buffer_1
  assign DATA_BUS = B_O ? register_2_q : 16'bz;  // Controlled_Buffer controlled_buffer_2
  Demultiplexer #(.select(3)) demultiplexer_1 (
    .out1(PC_O), .out2(A_O), .out3(B_O), .out5(IR_O), .out6(ADR_O), .out7(R_O), .in(LESE_SKRIVE_TIL_BUSS),
    .sel(output_register_selection));  // open: out0, out4
  assign DATA_BUS = PC_O ? counter_1_1_adressout : 16'bz;  // Controlled_Buffer controlled_buffer_3
  Demultiplexer #(.select(3)) demultiplexer_2 (
    .out1(PC_W), .out2(A_W), .out3(B_W), .out5(IR_W), .out6(ADR_W), .out7(R_W), .in(1'b1),
    .sel(Write_register_selection));  // open: out0, out4
  Register #(.width(16)) register_3 (.D(DATA_BUS), .en(ADR_W), .clk(CLK), .Q(register_3_q));  // open: clr
  counter_1 counter_1_1 (.DataInn(DATA_BUS), .WriteEnable(CLK), .AdressOut(counter_1_1_adressout));  // open: CLK
  assign DATA_BUS = ADR_O ? register_3_q : 16'bz;  // Controlled_Buffer controlled_buffer_4
  RAM #(.addrWidth(16), .dataWidth(16)) ram_1 (
    .addr(register_3_q), .we(R_W), .oe(R_O), .clk(CLK), .din(DATA_BUS), .dout(ram_1_dout));
  assign DATA_BUS = R_O ? ram_1_dout : 16'bz;  // Controlled_Buffer controlled_buffer_5

  // Notes on the sheet:
  //   A_register
  //   B_register
  //   ADR Register
  //   000 = ingenting
  //   001 = PC(program counter
  //   010 = A(registerA)
  //   011 = B(registerB)
  //   110=ADR (Adresse)
  //   111 = RAM
  //   101 = IR (Instruction Register)
  //   Problem med logisim når man endrer signaler (trykker på knapper for å aktivere bO må man også trykke knapp for å aktivere A out først som fører til error
  //   NOTE Dette er ikke et problem hvis man gir alle verdiene samtidig som datamaskinen kommer itl å gjøre
  //   Løsning ha et eget signal som er deaktiver når man putter inn verdiene for hvilke registere man bruker slik at flere registere ikke outputter verdier samtidig og man får error
endmodule

module counter_1 (
  input  [15:0] DataInn,
  input  CLK,
  input  WriteEnable,
  output [15:0] AdressOut
);

  wire not_1_out;
  wire [15:0] adder_1_out, controlled_buffer_1_out, register_2_q;

  assign controlled_buffer_1_out = WriteEnable ? DataInn : 16'bz;  // Controlled_Buffer controlled_buffer_1
  not not_1 (not_1_out, WriteEnable);
  Register #(.width(16)) register_1 (.D(controlled_buffer_1_out), .en(CLK), .clk(CLK), .Q(AdressOut));  // open: clr
  assign controlled_buffer_1_out = not_1_out ? adder_1_out : 16'bz;  // Controlled_Buffer controlled_buffer_2
  Register #(.width(16)) register_2 (.Q(register_2_q));  // open: D, en, clk, clr
  Adder #(.width(16)) adder_1 (.a(register_2_q), .b(AdressOut), .out(adder_1_out), .cin(1'b1));  // open: cout

  // Notes on the sheet:
  //   Vil bare adderen det samme registert med en carry inn på 1
  //   Write enbale på velger jump ellers inkrementeres pc med 1 etter klokka
  //   PC (Program counter) målet er et register som teller oppover med 1 hver rising edge. Og man kan sette Datainn når man gjennomfører en jump command
endmodule

module control_unit2 (
  input  SumO,
  input  CountJump,
  input  CountO,
  input  CountE,
  input  BW,
  input  BO,
  input  IRW,
  input  IRO,
  input  AW,
  input  AO,
  input  [3:0] Instruction,
  input  in_12,
  input  [8:0] in_13,
  output [7:0] out_14
);

  wire CLK, CLK1, not_2_out, not_3_out, not_4_out, registere_2_1_ir_w, RESET;
  wire [2:0] counter_1_q, current_clock_3_bit, O_register_selection, W_register_selection;
  wire [7:0] demultiplexer_1_out0;
  wire [15:0] register_1_q, registere_2_1_data_bus;

  Clock clock_1 (.out(CLK1));
  not not_1 (CLK, CLK1);
  Counter #(.max('h7), .width(3)) counter_1 (
    .clr(RESET), .up(1'b1), .count(CLK1), .clk(1'b1), .Q(counter_1_q));  // open: load, D, carry
  Counter #(.max('h7), .width(3)) counter_2 (
    .clr(RESET), .load(not_2_out), .up(1'b1), .clk(CLK), .Q(current_clock_3_bit));  // open: count, D, carry
  not not_2 (not_2_out, 1'b1);
  Demultiplexer #(.select(3)) demultiplexer_1 (
    .out0(demultiplexer_1_out0[0]), .out1(demultiplexer_1_out0[1]), .out2(demultiplexer_1_out0[2]),
    .out3(demultiplexer_1_out0[3]), .out4(demultiplexer_1_out0[4]), .out5(demultiplexer_1_out0[5]),
    .out6(demultiplexer_1_out0[6]), .out7(demultiplexer_1_out0[7]), .in(1'b1), .sel(current_clock_3_bit));
  Register #(.width(16)) register_1 (
    .D(registere_2_1_data_bus), .en(registere_2_1_ir_w), .clk(CLK1), .Q(register_1_q));  // open: clr
  registere_2 registere_2_1 (
    .LESE_SKRIVE_TIL_BUSS(in_12), .CLK(CLK1), .output_register_selection(O_register_selection),
    .Write_register_selection(W_register_selection), .IR_W(registere_2_1_ir_w),
    .DATA_BUS(registere_2_1_data_bus));  // open: IR_O
  ROM #(.addrWidth(12), .dataWidth(10)) rom_1 (
    .addr({Instruction, demultiplexer_1_out0}),
    .data({SumO, CountJump, CountO, CountE, BW, BO, IRW, IRO, AW, AO}));
  ROM #(.addrWidth(9)) rom_2 (.addr(in_13), .data(out_14));
  assign O_register_selection = out_14[4] ? out_14[7:5] : 3'bz;  // Controlled_Buffer controlled_buffer_1
  assign O_register_selection = out_14[0] ? out_14[3:1] : 3'bz;  // Controlled_Buffer controlled_buffer_2
  alu_1 alu_1_1 ();  // open: WALUa, CLK, WALUb, DATA, cIn, InstrBus, LSR, cFlag, eFlag, aluOut, nFlag, zFlag
  not not_3 (not_3_out, out_14[4]);
  not not_4 (not_4_out, out_14[0]);
  assign W_register_selection = not_3_out ? out_14[7:5] : 3'bz;  // Controlled_Buffer controlled_buffer_3
  assign W_register_selection = not_4_out ? out_14[3:1] : 3'bz;  // Controlled_Buffer controlled_buffer_4

  // Notes on the sheet:
  //   Instruksjonsett:
  //   0001 = Move (reg1, reg2)
  //   1 = output 0 = Write
  //   Instruksjons format( instruksjon 4 bit - timing 3 bit - register 3 bit 
  //   Mikro instruksjon ----, 000 = 001,1, 110,0
  //   Mikro instruksjon laste pc til ram ----, 000 = 001, 1, 111,0
  //   000 = ingenting
  //   001 = PC(program counter
  //   010 = A(registerA)
  //   011 = B(registerB)
  //   110=ADR (Adresse)
  //   111 = RAM
  //   Mikro instruksjon laste instruction til ir ----. 010 = 111,1 101,0
  //   101 = IR (Instruction Register)
  //   Et problem med designet mitt er at man bare kan skrive til 1 register hver syklus
  //   La meg skrive dette programmet og se om det funker
  //   Instruction Register
  //   Mikro instruksjon laste pc til ram ----, 000 = 001, 1, 111,0
  //   Mikro instruksjon laste instruction til ir ----. 001 = 111,1 101,0
  //   3e
  //   contents of rom_2 (hex, n*v repeats v):
  //   3e fa 6*0 3e fa 6*0 3e fa 6*0 3e fa 6*0 3e fa 6*0 3e fa 6*0 3e fa 6*0 3e fa 6*0 3e fa 6*0 3e fa 6*0
  //   3e fa 6*0 3e fa 6*0 3e fa 6*0 3e fa 6*0 3e fa 6*0 3e fa 6*0 3e fa 6*0 3e fa 6*0 3e fa 6*0 3e fa 6*0
  //   3e fa 6*0 3e fa 6*0 3e fa 6*0 3e fa 6*0 3e fa 6*0 3e fa 6*0 3e fa 6*0 3e fa 6*0 3e fa 6*0 3e fa 6*0
  //   3e fa 6*0 3e fa 6*0 3e fa 6*0 3e fa 6*0 3e fa 6*0 3e fa 6*0 3e fa 6*0 3e fa 6*0 3e fa 6*0 3e fa 6*0
  //   3e fa 6*0 3e fa 6*0 3e fa 6*0 3e fa 6*0 3e fa 6*0 3e fa 6*0 3e fa 6*0 3e fa 6*0 3e fa 6*0 3e fa 6*0
  //   3e fa 6*0 3e fa 6*0 3e fa 6*0 3e fa 6*0 3e fa 6*0 3e fa 6*0 3e fa 6*0 3e fa 6*0 3e fa 6*0 3e fa 6*0
  //   3e fa 6*0 3e fa 6*0 3e fa 6*0 3e fa
  //   fa
  //   2 output per register 1 for out 1 for write
endmodule

module ALU_v3 (
  input  CLK,
  input  [15:0] DATA,
  input  [15:0] ALU_REGISTER,
  input  cIn,
  input  [1:0] InstrBus,
  output cFlag,
  output nFlag,
  output [15:0] SUM,
  output zFlag
);

  wire demultiplexer_1_out0, demultiplexer_1_out1, demultiplexer_1_out2, demultiplexer_1_out3;
  wire [15:0] adder_1_out, nand_1_out, xor_1_out;

  nor nor_1 (zFlag, SUM[8], nFlag, SUM[14], SUM[13], SUM[12], SUM[11], SUM[10], SUM[9], SUM[7], SUM[6], SUM[5], SUM[4], SUM[3], SUM[2], SUM[1], SUM[0]);
  assign {nFlag, SUM[14:0]} = demultiplexer_1_out0 ? {1'b0, DATA[15:1]} : 16'bz;  // Controlled_Buffer controlled_buffer_1
  assign xor_1_out = DATA ^ ALU_REGISTER;  // XOR_Gate xor_1, 16 bits wide
  assign {nFlag, SUM[14:0]} = demultiplexer_1_out3 ? xor_1_out : 16'bz;  // Controlled_Buffer controlled_buffer_2
  assign nand_1_out = ~(DATA & ALU_REGISTER);  // NAND_Gate nand_1, 16 bits wide
  assign {nFlag, SUM[14:0]} = demultiplexer_1_out1 ? nand_1_out : 16'bz;  // Controlled_Buffer controlled_buffer_3
  assign {nFlag, SUM[14:0]} = demultiplexer_1_out2 ? adder_1_out : 16'bz;  // Controlled_Buffer controlled_buffer_4
  Adder #(.width(16)) adder_1 (.a(DATA), .b(ALU_REGISTER), .out(adder_1_out), .cin(cIn), .cout(cFlag));
  Demultiplexer #(.select(2)) demultiplexer_1 (
    .out0(demultiplexer_1_out0), .out1(demultiplexer_1_out1), .out2(demultiplexer_1_out2),
    .out3(demultiplexer_1_out3), .in(1'b1), .sel(InstrBus));

  assign SUM[15] = nFlag;

  // Other names for the same wires on the sheet: DATA_BUSS[15:0] = DATA

  // Notes on the sheet:
  //   Even flag kan legges til
  //   00 = R_shift
  //   01 = nand
  //   10 = adder
  //   11 = Xor
endmodule

module CPU_v3 (
);

  wire ADR_O, ADR_W, ALU_W, and_1_out, and_2_out, and_3_out, and_4_out, and_5_out, and_6_out, and_7_out,
       and_8_out, and_9_out, and_10_out, and_11_out, and_12_out, and_13_out, and_14_out, and_15_out,
       and_16_out, and_17_out, and_18_out, and_20_out, and_21_out, and_22_out, and_23_out, button_1_out,
       button_2_out, CarryIn, demultiplexer_1_out0, demultiplexer_1_out1, demultiplexer_1_out2,
       demultiplexer_1_out7, demultiplexer_2_out0, demultiplexer_2_out1, demultiplexer_2_out2,
       demultiplexer_2_out7, demultiplexer_3_out0, demultiplexer_3_out1, demultiplexer_3_out2,
       demultiplexer_3_out7, IR_W, klok, not_1_out, PC_INCREMENT, PC_O, PC_W, R_O, R_W, SetFlag, SP_O, SP_W,
       SUM_O, X_O, X_W, Y_O, Y_W, Z_O, Z_W;
  wire [0:0] control_data;
  wire [1:0] ALU_INSTR;
  wire [2:0] alu_v3_1_cflag, counter_2_q, Flag;
  wire [6:5] ALU_data;
  wire [7:0] rom1_data;
  wire [15:0] ALU_REGISTER_q, alu_v3_1_sum, controlled_buffer_1_out, controlled_buffer_10_out, counter_1_q,
       ram_1_dout, register_1_q, register_2_q, register_3_q, register_4_q, register_5_q, register_6_q,
       register_7_q, SUM_register_q, undriven;

  Register #(.width(16)) register_1 (.D(controlled_buffer_1_out), .en(X_W), .clk(klok), .Q(register_1_q));  // open: clr
  Register #(.width(16)) register_2 (.D(controlled_buffer_1_out), .en(Y_W), .clk(klok), .Q(register_2_q));  // open: clr
  Register #(.width(16)) register_3 (.D(controlled_buffer_1_out), .en(Z_W), .clk(klok), .Q(register_3_q));  // open: clr
  Register #(.width(16)) register_4 (.D(undriven), .en(Z_W), .clk(klok), .Q(register_4_q));  // open: clr
  Register #(.width(16)) register_5 (
    .D(controlled_buffer_1_out), .en(SP_W), .clk(klok), .Q(register_5_q));  // open: clr
  assign controlled_buffer_1_out = X_O ? register_1_q : 16'bz;  // Controlled_Buffer controlled_buffer_1
  assign controlled_buffer_1_out = Y_O ? register_2_q : 16'bz;  // Controlled_Buffer controlled_buffer_2
  assign controlled_buffer_1_out = Z_O ? register_3_q : 16'bz;  // Controlled_Buffer controlled_buffer_3
  Controlled_Buffer #(.width(16)) controlled_buffer_4 (.in(register_4_q), .en(Z_O));  // open: out
  assign controlled_buffer_1_out = SP_O ? register_5_q : 16'bz;  // Controlled_Buffer controlled_buffer_5
  Button button_1 (.out(button_1_out));
  Counter #(.max('hffff), .width(16)) counter_1 (
    .clr(button_1_out), .load(PC_W), .up(1'b1), .count(PC_INCREMENT), .clk(klok),
    .D(controlled_buffer_1_out), .Q(counter_1_q));  // open: carry
  Register #(.width(16)) ALU_REGISTER (
    .D(controlled_buffer_1_out), .en(ALU_W), .clk(klok), .Q(ALU_REGISTER_q));  // open: clr
  Register #(.width(16)) register_6 (
    .D(controlled_buffer_1_out), .en(ADR_W), .clk(klok), .Q(register_6_q));  // open: clr
  assign controlled_buffer_1_out = SUM_O ? SUM_register_q : 16'bz;  // Controlled_Buffer controlled_buffer_6
  RAM #(.addrWidth(16), .dataWidth(16), .trigger("high"), .\type ("nonvolatile")) ram_1 (
    .addr(register_6_q), .we(R_W), .oe(1'b1), .din(controlled_buffer_1_out), .dout(ram_1_dout));
  Register #(.width(16)) InverteringsRegister ();  // open: D, en, clk, Q, clr
  assign controlled_buffer_1_out = ADR_O ? register_6_q : 16'bz;  // Controlled_Buffer controlled_buffer_7
  Register #(.width(16)) SUM_register (.D(alu_v3_1_sum), .en(1'b1), .clk(klok), .Q(SUM_register_q));  // open: clr
  assign controlled_buffer_1_out = PC_O ? counter_1_q : 16'bz;  // Controlled_Buffer controlled_buffer_8
  ALU_v3 alu_v3_1 (
    .DATA(controlled_buffer_1_out), .ALU_REGISTER(ALU_REGISTER_q), .cIn(CarryIn), .InstrBus(ALU_INSTR),
    .cFlag(alu_v3_1_cflag[0]), .nFlag(alu_v3_1_cflag[1]), .SUM(alu_v3_1_sum), .zFlag(alu_v3_1_cflag[2]));  // open: CLK
  assign controlled_buffer_1_out = R_O ? ram_1_dout : 16'bz;  // Controlled_Buffer controlled_buffer_9
  Register #(.trigger("high"), .width(16)) register_7 (
    .D(controlled_buffer_1_out), .en(IR_W), .clk(klok), .Q(register_7_q));  // open: clr
  Clock clock_1 (.out(klok));
  assign controlled_buffer_10_out = 1'b1 ? register_7_q : 16'bz;  // Controlled_Buffer controlled_buffer_10
  Counter #(.max('h7), .width(3)) counter_2 (
    .clr(button_2_out), .up(1'b1), .count(1'b1), .clk(not_1_out), .Q(counter_2_q));  // open: load, D, carry
  Button button_2 (.out(button_2_out));
  not not_1 (not_1_out, klok);
  // XOR_Gate xor_1 is placed but not wired
  // XOR_Gate xor_2 is placed but not wired
  Register #(.width(3)) register_8 (.D(alu_v3_1_cflag), .en(SetFlag), .clk(klok), .Q(Flag));  // open: clr
  ROM #(.addrWidth(7)) rom1 (.addr({controlled_buffer_10_out[3:0], counter_2_q}), .data(rom1_data));
  Demultiplexer #(.select(3)) demultiplexer_1 (
    .out0(demultiplexer_1_out0), .out1(demultiplexer_1_out1), .out2(demultiplexer_1_out2),
    .out7(demultiplexer_1_out7), .in(1'b1), .sel(controlled_buffer_10_out[9:7]));  // open: out3, out4, out5, out6
  Demultiplexer #(.select(3)) demultiplexer_2 (
    .out0(demultiplexer_2_out0), .out1(demultiplexer_2_out1), .out2(demultiplexer_2_out2),
    .out7(demultiplexer_2_out7), .in(1'b1), .sel(controlled_buffer_10_out[12:10]));  // open: out3, out4, out5, out6
  Demultiplexer #(.select(3)) demultiplexer_3 (
    .out0(demultiplexer_3_out0), .out1(demultiplexer_3_out1), .out2(demultiplexer_3_out2),
    .out7(demultiplexer_3_out7), .in(1'b1), .sel(controlled_buffer_10_out[15:13]));  // open: out3, out4, out5, out6
  or or_1 (X_W, and_1_out, and_3_out, and_5_out);
  and and_1 (and_1_out, demultiplexer_1_out0, rom1_data[0]);
  and and_2 (and_2_out, demultiplexer_1_out0, rom1_data[1]);
  and and_3 (and_3_out, demultiplexer_2_out0, rom1_data[2]);
  and and_4 (and_4_out, demultiplexer_2_out0, rom1_data[3]);
  and and_5 (and_5_out, demultiplexer_3_out0, rom1_data[4]);
  and and_6 (and_6_out, demultiplexer_3_out0, rom1_data[5]);
  or or_2 (X_O, and_2_out, and_4_out, and_6_out);
  or or_3 (Y_W, and_7_out, and_9_out, and_11_out);
  and and_7 (and_7_out, demultiplexer_1_out1, rom1_data[0]);
  and and_8 (and_8_out, demultiplexer_1_out1, rom1_data[1]);
  and and_9 (and_9_out, demultiplexer_2_out1, rom1_data[2]);
  and and_10 (and_10_out, demultiplexer_2_out1, rom1_data[3]);
  and and_11 (and_11_out, demultiplexer_3_out1, rom1_data[4]);
  and and_12 (and_12_out, demultiplexer_3_out1, rom1_data[5]);
  or or_4 (Y_O, and_8_out, and_10_out, and_12_out);
  and and_13 (and_13_out, demultiplexer_1_out2, rom1_data[0]);
  and and_14 (and_14_out, demultiplexer_1_out2, rom1_data[1]);
  and and_15 (and_15_out, demultiplexer_2_out2, rom1_data[2]);
  and and_16 (and_16_out, demultiplexer_2_out2, rom1_data[3]);
  and and_17 (and_17_out, demultiplexer_3_out2, rom1_data[4]);
  or or_5 (Z_W, and_13_out, and_15_out, and_17_out);
  and and_18 (and_18_out, demultiplexer_3_out2, rom1_data[5]);
  or or_6 (Z_O, and_14_out, and_16_out, and_18_out);
  and and_19 (SP_W, demultiplexer_1_out7, rom1_data[0]);
  ROM #(.addrWidth(7)) control (
    .addr({controlled_buffer_10_out[3:0], counter_2_q}),
    .data({PC_INCREMENT, IR_W, R_O, R_W, ADR_O, ADR_W, PC_O, control_data[0]}));
  and and_20 (and_20_out, demultiplexer_3_out7, rom1_data[5]);
  or or_7 (SP_O, and_20_out, and_21_out);
  ROM #(.addrWidth(7)) ALU (
    .addr({controlled_buffer_10_out[3:0], counter_2_q}),
    .data({SetFlag, ALU_data, CarryIn, ALU_W, SUM_O, ALU_INSTR}));
  and and_21 (and_21_out, demultiplexer_2_out7, rom1_data[3]);
  and and_22 (and_22_out, Flag[2], ALU_data[5]);
  or or_8 (PC_W, and_22_out, and_23_out, control_data[0]);
  and and_23 (and_23_out, Flag[1], ALU_data[6]);

  // Notes on the sheet:
  //   000 = ingenting
  //   001 = PC(program counter
  //   010 = A(registerA)
  //   011 = B(registerB)
  //   101 = IR (Instruction Register)
  //   110=ADR (Adresse)
  //   111 = RAM
  //   NOTE Dette er ikke et problem hvis man gir alle verdiene samtidig som datamaskinen kommer itl å gjøre
  //   Problem med logisim når man endrer signaler (trykker på knapper for å aktivere bO må man også trykke knapp for å aktivere A out først som fører til error
  //   Løsning ha et eget signal som er deaktiver når man putter inn verdiene for hvilke registere man bruker slik at flere registere ikke outputter verdier samtidig og man får error
  //   0402 = move(regx, regy)
  //   0102 = move regz, regx
  //   4401 = add(regx, regy, regz)
  //   0400 tar W register x, O register y
  //   Eksempel på en add instruksjon i ram (1000000 - 000 - 001 - 010)
  //   Instruksjonen over vil ta verdien i register y + verdien i register z og legge det i x
  //   Eksempel instruksjon ADD(rd, rs1, rs2)
  //   Opcode for Add = 1000000
  //   X register adresse = 000
  //   Y register adresse = 001
  //   Z register adresse = 010
  //   Register 1
  //   Register 2
  //   Register 3
  //   Midlertidlig for å slippe å skrive inn mer i ROM
  //   contents of rom1 (hex, n*v repeats v):
  //   10*0 9 7*0 8 20 1 6*0 1 6*0 8 8 1 5*0 8 20 14*0 8 7*0 20 20 0 8 1 0 0 0 8 25*0 8 0 1 5*0 20 0 8 0 0
  //   0 8 0 1
  //   contents of control (hex, n*v repeats v):
  //   6 e0 6*0 6 e0 6*0 6 e0 6*0 6 e0 6 a0 4*0 6 e0 6*0 6 e0 4 20 4*0 6 e0 6*0 6 e0 1 5*0 6 e0 6*0 6 e0
  //   6*0 6 e0 6 20 4*0 6 e0 6 21 4*0 6 e0 6 a0 0 4 20 0 6 e0 6 a0 0 4 10 0 6 e0 6*0 6 e0 6 20
  //   contents of ALU (hex, n*v repeats v):
  //   18*0 8 2 4 13*0 8 11 4 29*0 8 1 c 92 4 0 0 0 20 8*0 20 15*0 8 2 4 5*0 8 2 4 4*0 8 12 4 6*0 40
  //   Eksempel på en add instruksjon i ram (1000000 - 000 - 001 - 010) (rekkefølgen er motsatt
  //   Instruksjonen over vil ta verdien i register y + verdien i register z og legge det i x
  //   De 6 første bitsa er i rekkefølge register 1 W, register 1 O, register 2 W, register 2O, register 3 W, register 3O
  //   Eksempel instruksjon ADD(rd, rs1, rs2)
  //   Opcode for Add = 1000000
  //   MOVE instruksjon MOV(000, 001, 000, 0000010
  //   s2
  //   Vil kopiere verdien i YR inn i XR
  //   s1
  //   rd
  //   opcode
  //   Jump if negative
  //   X register adresse = 000
  //   Y register adresse = 001
  //   Z register adresse = 010
  //   jumpif zerobit
  //   R står for ram
  //   når t-state/kolle er 0 pc_O, adr_W
  //   når t-state/klokke er 1 M_O IR_W
  //   Når t state/kolle er 10 PC_INCREMENT
  //   output = 00000110
  //   output = 01100000
  //   06
  //   60
  //   output  = 10000000
  //   80
  //   Instruksjon move
  //   når t-state = 2,
  //   reg 1 wirte, reg 2 o
endmodule

module breadboardtest (
);

  wire n7404_1_pin8, n7404_1_pin10, n7404_1_pin11, n7404_1_pin12, n7404_1_pin13;

  _7404 u_7404_1 (
    .pin13(n7404_1_pin13), .pin12(n7404_1_pin12), .pin11(n7404_1_pin11), .pin10(n7404_1_pin10),
    .pin8(n7404_1_pin8));  // open: pin1, pin2, pin3, pin4, pin5, pin6, pin9
  _74165 #(.VccGndPorts("true")) u_74165_1 ();  // open: pin1, pin2, pin3, pin4, pin5, pin6, pin7, pin8, pin16, pin15, pin14, pin13, pin12, pin11, pin10, pin9
  _7419 u_7419_1 ();  // open: pin1, pin2, pin3, pin4, pin5, pin6, pin13, pin12, pin11, pin10, pin9, pin8
  _7447 u_7447_1 ();  // open: pin1, pin2, pin3, pin4, pin5, pin6, pin7, pin15, pin14, pin13, pin12, pin11, pin10, pin9
endmodule
