// Logisim project alu_register_integrasjon.circ as structural Verilog: 4 circuits, main circuit main
module main (
  input  [15:0] in_1,
  input  in_2,
  input  in_3,
  input  [15:0] in_4,
  input  in_5
);

  wire alu_1_nflag, alu_1_zflag, AO, CLK, registere_1_p8;
  wire [3:0] Instruksjon, Instruskjon;
  wire [15:0] ALUOUT, controlled_buffer_1_out, DATABUSSIN, ram_1_dout, registere_1_p7;

  Clock clock_1 (.out(CLK));
  RAM #(.addrWidth(15), .dataWidth(16)) ram_1 (
    .addr(in_4[14:0]), .we(in_5), .oe(in_3), .clk(CLK), .din(in_1), .dout(ram_1_dout));
  ControlUnit controlunit_1 (
    .CLK(CLK), .AO(AO), .Instruction(Instruksjon));  // open: SumO, Jump, CountO, CountE, BW, BO, IRW, IRO, AW
  // Registere registere_1: pin names not known; wires that end beside it: DATABUSSIN, AO, Instruskjon, CLK, in_4, ALUOUT, registere_1_p7, registere_1_p8
  ALU alu_1 (
    .CLK(CLK), .nFlag(alu_1_nflag), .aluOut(ALUOUT), .zFlag(alu_1_zflag));  // open: Ain, Bin, carryIn, in_5, CLAND, CLADD, CLXOR, LSR, cFlag, eFlag
  assign controlled_buffer_1_out = in_2 ? registere_1_p7 : 16'bz;  // Controlled_Buffer controlled_buffer_1
  // Pins of 15 and 16 bits meet at in_4

  // Other names for the same wires on the sheet: ADRESSEBUSS[15:0] = in_4; DATABUSS[15:0] = in_1; RI = in_5;
  //   RO = in_3

  // Notes on the sheet:
  //   Registere kunne egt ha vært en god Main
  //   Skulle ikke aluOut bare gjennom databussen? Blir mye mindre kabling, selv om kanskje fler sykluser per instruksjon
  //   PINS som er på høyre side er outpus!!!
endmodule

module Registere (
  input  AO,
  input  [3:0] SkalTilDekoding,
  input  CLK,
  input  [15:0] ADRESSEIN,
  input  AW,
  input  IRO,
  input  [15:0] DATAIN,
  input  [11:0] ID,
  input  IRW,
  input  BO,
  input  BW,
  input  DATAINENABLE,
  input  JUMP,
  input  CountE,
  input  CounterO,
  input  SumO,
  input  [15:0] SumIN,
  output [15:0] DATAOUT,
  output [15:0] ADRESSEOUT
);

  wire and_1_out, not_1_out, not_2_out, not_3_out, not_4_out, not_5_out, not_7_out, not_8_out, undriven,
       undriven_2, undriven_3, undriven_4, undriven_5, undriven_6, undriven_8, undriven_9;
  wire [15:0] controlled_buffer_1_out, controlled_buffer_2_out, counter_1_q, RAM, register_1_q, register_2_q,
       register_3_q, register_4_q, register_5_q, register_6_q, register_7_q, register_8_q, register_9_q,
       transistor_1_out, transistor_2_out, transistor_7_out, undriven_7;

  Register #(.width(16)) register_1 (.D(controlled_buffer_1_out), .en(BW), .clk(CLK), .Q(register_1_q));  // open: clr
  assign controlled_buffer_1_out = BW ? DATAOUT : 16'bz;  // Controlled_Buffer controlled_buffer_1
  Register #(.width(16)) register_2 (.D(DATAOUT), .en(undriven_2), .clk(CLK), .Q(register_2_q));  // open: clr
  Register #(.width(16)) register_3 (.D(DATAOUT), .en(undriven), .clk(CLK), .Q(register_3_q));  // open: clr
  Register #(.width(16)) register_4 (.D(controlled_buffer_2_out), .en(AW), .clk(CLK), .Q(register_4_q));  // open: clr
  assign controlled_buffer_2_out = AW ? DATAOUT : 16'bz;  // Controlled_Buffer controlled_buffer_2
  Register #(.width(16)) register_5 (.D(SumIN), .en(1'b1), .clk(CLK), .Q(register_5_q));  // open: clr
  Register #(.width(16)) register_6 (.D(RAM), .en(undriven_3), .clk(CLK), .Q(register_6_q));  // open: clr
  assign DATAOUT = AO ? register_4_q : 16'bz;  // Controlled_Buffer controlled_buffer_3
  assign DATAOUT = BO ? register_1_q : 16'bz;  // Controlled_Buffer controlled_buffer_4
  not not_1 (not_1_out, undriven_4);
  Transistor #(.width(16)) transistor_1 (.in(register_2_q), .out(transistor_1_out), .gate(not_1_out));
  not not_2 (not_2_out, undriven_5);
  Transistor #(.width(16)) transistor_2 (.in(register_3_q), .out(transistor_2_out), .gate(not_2_out));
  not not_3 (not_3_out, SumO);
  Transistor #(.width(16)) transistor_3 (.in(register_5_q), .out(DATAOUT), .gate(not_3_out));
  not not_4 (not_4_out, undriven_6);
  Transistor #(.width(16)) transistor_4 (.in(register_6_q), .gate(not_4_out));  // open: out
  Register #(.width(16)) register_7 (.D(DATAOUT), .en(IRW), .clk(CLK), .Q(register_7_q));  // open: clr
  not not_5 (not_5_out, IRO);
  assign ADRESSEIN[15:12] = ~4'b1111;  // NOT_Gate not_6, 4 bits wide
  Transistor #(.width(16)) transistor_5 (.in(register_7_q), .out({SkalTilDekoding, ADRESSEIN[11:0]}), .gate(not_5_out));
  buf and_1 (and_1_out, CLK);  // AND_Gate
  Register #(.width(16)) register_8 (.D(DATAIN), .en(DATAINENABLE), .clk(CLK), .Q(register_8_q));  // open: clr
  Counter #(.max('hffff), .width(16)) counter_1 (
    .load(JUMP), .clk(and_1_out), .D(DATAOUT), .Q(counter_1_q));  // open: clr, up, count, carry
  assign DATAOUT = DATAINENABLE ? register_8_q : 16'bz;  // Controlled_Buffer controlled_buffer_5
  not not_7 (not_7_out, CounterO);
  Transistor #(.width(16)) transistor_6 (.in(counter_1_q), .out(ADRESSEIN), .gate(not_7_out));
  Register #(.width(16)) register_9 (.D(undriven_7), .en(undriven_8), .clk(CLK), .Q(register_9_q));  // open: clr
  not not_8 (not_8_out, undriven_9);
  Transistor #(.width(16)) transistor_7 (.in(register_9_q), .out(transistor_7_out), .gate(not_8_out));

  assign ADRESSEOUT = ADRESSEIN;

  // Other names for the same wires on the sheet: ADRESSEBUSS[15:0] = ADRESSEIN; DATABUSS[15:0] = DATAOUT;
  //   DATABUSSIN[15:0] = DATAIN

  // Notes on the sheet:
  //   Under constrution!!
  //   Sparer vi ikke sykluser på  å  loade direkte til databuss? Blir mindre komplisert, siden vi ikke har snakket om noe cashing
  //   Liten buffer siden det kommer feil når input pin er direkte koblet med en output pin
endmodule

module ALU (
  input  [15:0] Ain,
  input  [15:0] Bin,
  input  CLK,
  input  carryIn,
  input  [1:0] in_5,
  input  CLAND,
  input  CLADD,
  input  CLXOR,
  input  LSR,
  output cFlag,
  output eFlag,
  output nFlag,
  output [15:0] aluOut,
  output zFlag
);

  wire and_2_out, and_4_out, and_5_out, and_6_out, multiplexer_1_out, NAME;
  wire [14:0] or_1_out;
  wire [15:0] adder_1_out, and_1_out, and_3_out, nand_1_out, not_1_out, xor_1_out;
  wire [15:1] controlled_buffer_1_out;

  assign xor_1_out = Ain ^ Bin;  // XOR_Gate xor_1, 16 bits wide
  assign and_1_out = {controlled_buffer_1_out, eFlag} & not_1_out;  // AND_Gate and_1, 16 bits wide
  assign {controlled_buffer_1_out, eFlag} = and_6_out ? xor_1_out : 16'bz;  // Controlled_Buffer controlled_buffer_1
  assign nand_1_out = ~(Bin & Ain);  // NAND_Gate nand_1, 16 bits wide
  assign {controlled_buffer_1_out, eFlag} = and_5_out ? adder_1_out : 16'bz;  // Controlled_Buffer controlled_buffer_2
  assign {controlled_buffer_1_out, eFlag} = and_4_out ? nand_1_out : 16'bz;  // Controlled_Buffer controlled_buffer_3
  assign {nFlag, or_1_out} = and_1_out | and_3_out;  // OR_Gate or_1, 16 bits wide
  and and_2 (and_2_out, CLK, NAME);
  assign and_3_out = {1'b0, controlled_buffer_1_out} & {16{LSR}};  // AND_Gate and_3, 16 bits wide
  Register #(.trigger("falling"), .width(16)) register_1 (
    .D({nFlag, or_1_out}), .en(1'b1), .clk(and_2_out), .Q(aluOut));  // open: clr
  Adder #(.width(16)) adder_1 (.a(Bin), .b(Ain), .out(adder_1_out), .cin(carryIn), .cout(cFlag));
  assign not_1_out = ~{16{LSR}};  // NOT_Gate not_1, 16 bits wide
  and and_4 (and_4_out, CLK, CLAND);
  and and_5 (and_5_out, CLK, CLADD);
  and and_6 (and_6_out, CLK, CLXOR);
  Multiplexer #(.select(2)) multiplexer_1 (.out(multiplexer_1_out), .sel(in_5));  // open: in0, in1, in2, in3
  nor nor_1 (zFlag, or_1_out[8], nFlag, or_1_out[14], or_1_out[13], or_1_out[12], or_1_out[11], or_1_out[10], or_1_out[9], or_1_out[7], or_1_out[6], or_1_out[5], or_1_out[4], or_1_out[3], or_1_out[2], or_1_out[1], or_1_out[0]);
  or or_2 (NAME, CLAND, CLADD, CLXOR);

  // Notes on the sheet:
  //   Even flag kan slettes om den ikke trengs
  //   Fjern and gates og bruk multiplex
  //   Dette er logikk som skal passe på at output ikke blir error
endmodule

module ControlUnit (
  input  CLK,
  input  SumO,
  input  Jump,
  input  CountO,
  input  CountE,
  input  BW,
  input  BO,
  input  IRW,
  input  IRO,
  input  AW,
  input  AO,
  input  [3:0] Instruction
);

  wire CLK_t, not_1_out, RESET;
  wire [2:0] counter_1_q;
  wire [7:0] demultiplexer_1_out0;

  Counter #(.max('h7), .width(3)) counter_1 (
    .clr(RESET), .load(not_1_out), .up(1'b1), .clk(CLK_t), .Q(counter_1_q));  // open: count, D, carry
  not not_1 (not_1_out, 1'b1);
  not not_2 (CLK_t, CLK);
  Demultiplexer #(.select(3)) demultiplexer_1 (
    .out0(demultiplexer_1_out0[0]), .out1(demultiplexer_1_out0[1]), .out2(demultiplexer_1_out0[2]),
    .out3(demultiplexer_1_out0[3]), .out4(demultiplexer_1_out0[4]), .out5(demultiplexer_1_out0[5]),
    .out6(demultiplexer_1_out0[6]), .out7(demultiplexer_1_out0[7]), .in(1'b1), .sel(counter_1_q));
  ROM #(.addrWidth(12), .dataWidth(10)) rom_1 (
    .addr({Instruction, demultiplexer_1_out0}), .data({SumO, Jump, CountO, CountE, BW, BO, IRW, IRO, AW, AO}));
endmodule
